# Fritzing sketch CircuitDiagram (saved by Fritzing 0.9.3b)
breadboards: 1

parts:
  Part1 = Arduino Nano (Rev3.0)
  U1 = POT [package=alps_pot]
  U2 = POT [package=alps_pot]
  S1 = Pushbutton [package="[THT]"]
  S2 = Pushbutton [package="[THT]"]
  S3 = Pushbutton [package="[THT]"]
  R1 = Resistor [tolerance=±5% resistance=10k package=THT]
  R2 = Resistor [tolerance=±5% resistance=10k package=THT]
  R3 = Resistor [tolerance=±5% resistance=10k package=THT]
  Part2 = Ludus ProtoShield
  VCC1 = Battery
  VCC2 = Battery
  J1 = Basic Servo
  J2 = Basic Servo
  J3 = Basic Servo
  J4 = Basic Servo
  LED11 = LED - 5mm [color="White (6500K)" package="5 mm [THT]"]
  LED12 = LED - 5mm [color="White (6500K)" package="5 mm [THT]"]
  LED1 = LED - 5mm [color="White (6500K)" package="5 mm [THT]"]
  LED2 = LED - 5mm [color="White (6500K)" package="5 mm [THT]"]
  R5 = Resistor [tolerance=±5% resistance=22 package="1206 [SMD]"]
  LED3 = LED - 5mm [color="White (6500K)" package="5 mm [THT]"]
  LED9 = LED - 5mm [color="White (6500K)" package="5 mm [THT]"]
  LED7 = LED - 5mm [color="White (6500K)" package="5 mm [THT]"]
  R7 = Resistor [tolerance=±5% resistance=22 package="1206 [SMD]"]
  LED8 = LED - 5mm [color="White (6500K)" package="5 mm [THT]"]
  LED4 = LED - 5mm [color="White (6500K)" package="5 mm [THT]"]
  R9 = Resistor [tolerance=±5% resistance=22 package="1206 [SMD]"]
  R8 = Resistor [tolerance=±5% resistance=22 package="1206 [SMD]"]
  R6 = Resistor [tolerance=±5% resistance=22 package="1206 [SMD]"]
  LED5 = LED - 5mm [color="White (6500K)" package="5 mm [THT]"]
  LED10 = LED - 5mm [color="White (6500K)" package="5 mm [THT]"]
  R4 = Resistor [tolerance=±5% resistance=22 package="1206 [SMD]"]
  LED6 = LED - 5mm [color="White (6500K)" package="5 mm [THT]"]

nets:
  GND: Part1.GND, U1.E, U2.E, R1.Pin_0, R2.Pin_0, R3.Pin_0, Part2.GND, J1.gnd, J2.gnd, J3.gnd, J4.gnd
  N1: Part1.D2, S1.Pin_1, S1.Pin_2, R3.Pin_1
  N2: Part1.D3, S2.Pin_1, S2.Pin_2, R2.Pin_1
  N3: Part1.D4, S3.Pin_1, S3.Pin_2, R1.Pin_1
  5V: Part1.5V, U1.A, U2.A, S1.Pin_3, S1.Pin_4, S2.Pin_3, S2.Pin_4, S3.Pin_3, S3.Pin_4, Part2.VCC
  N4: Part1.A5, Part2.SCL
  N5: Part1.A4, Part2.SDA
  N6: Part1.A1, U1.S
  N7: Part1.A0, U2.S
  VCC: Part2.ANALOG_PWR_RAIL, J1.vcc, J2.vcc, J3.vcc, J4.vcc
  N8: Part2.A0, J1.pulse
  N9: Part2.A1, J2.pulse
  N10: Part2.A2, J3.pulse
  N11: Part2.A3, J4.pulse
  N12: Part2.AOUT2, VCC1.-
  N13: Part2.AOUT1, VCC2.+
  N14: VCC1.+, VCC2.-
  N15: LED11.cathode, R9.Pin_0
  N16: LED11.anode, LED12.cathode
  N17: LED12.anode, LED2.anode, LED8.anode, LED4.anode, LED10.anode, LED6.anode
  N18: LED1.cathode, R4.Pin_0
  N19: LED1.anode, LED2.cathode
  N20: R5.Pin_0, LED3.cathode
  N21: R5.Pin_1, R7.Pin_1, R9.Pin_1, R8.Pin_1, R6.Pin_1, R4.Pin_1
  N22: LED3.anode, LED4.cathode
  N23: LED9.cathode, R8.Pin_0
  N24: LED9.anode, LED10.cathode
  N25: LED7.cathode, R6.Pin_0
  N26: LED7.anode, LED8.cathode
  N27: R7.Pin_0, LED5.cathode
  N28: LED5.anode, LED6.cathode

notes:
  switch
  cont
  light
  save, load
  pretend this is PCA9685 16-Channel Servo Driver
  6v ~2000mAh
  5v 300mA
